// Logisim project cpu.circ as structural Verilog: 1 circuit, main circuit cpu
module cpu (
  input  clk,
  input  [31:0] INSTRUCTION,
  input  [31:0] READ_DATA,
  output [31:0] WRITE_ADDRESS,
  output [31:0] PROGRAM_COUNTER,
  output [31:0] ra,
  output [31:0] sp,
  output [31:0] t0,
  output [31:0] t1,
  output [31:0] t2,
  output [31:0] s0,
  output [31:0] s1,
  output [31:0] a0,
  output [31:0] tohost,
  output [3:0] WRITE_ENABLE,
  output [31:0] WRITE_DATA
);

  wire ASel, BrEq, BrLt, BrUn, BSel, comparator_1_eq, comparator_2_eq, comparator_3_eq, comparator_4_eq,
       comparator_5_eq, comparator_6_eq, comparator_7_eq, comparator_8_eq, comparator_9_eq, comparator_10_eq,
       comparator_11_eq, comparator_12_eq, CSRSel, CSRWen, is_lb, is_lh, is_lw, is_sb, is_sh, is_sw, MemRW,
       PCSel, RegWEn;
  wire [1:0] WBSel;
  wire [2:0] funct3, ImmSel;
  wire [3:0] ALUSel, multiplexer_3_out, multiplexer_5_out, multiplexer_6_out;
  wire [4:0] AddrA, AddrB, AddrD;
  wire [6:0] funct7, opcode;
  wire [31:0] adder_1_out, DataA, DMEM_WRITE_DATA, imme, multiplexer_1_out, multiplexer_2_out,
       multiplexer_4_out, multiplexer_9_out, multiplexer_10_out, multiplexer_11_out, PCforALU,
       READ_DATA_Byte, READ_DATA_Half_Word, WBResult;

  Multiplexer #(.enable("false"), .width(32)) multiplexer_1 (
    .in0(INSTRUCTION), .in1(32'h13), .out(multiplexer_1_out), .sel(PCSel));
  Adder #(.width(32)) adder_1 (.a(PROGRAM_COUNTER), .b(32'h4), .out(adder_1_out));  // open: cin, cout
  Register #(.width(32)) register_1 (
    .D(multiplexer_1_out), .en(1'b1), .clk(clk), .Q({funct7, AddrB, AddrA, funct3, AddrD, opcode}));  // open: clr
  Multiplexer #(.enable("false"), .width(32)) multiplexer_2 (
    .in0(adder_1_out), .in1(WRITE_ADDRESS), .out(multiplexer_2_out), .sel(PCSel));
  Register #(.width(32)) PC (.D(multiplexer_2_out), .en(1'b1), .clk(clk), .Q(PROGRAM_COUNTER));  // open: clr
  Comparator #(.mode("unsigned"), .width(7)) comparator_1 (
    .a(opcode), .b(7'b0000011), .eq(comparator_1_eq));  // open: gt, lt
  Comparator #(.mode("unsigned"), .width(3)) comparator_2 (
    .a(funct3), .b(3'b000), .eq(comparator_2_eq));  // open: gt, lt
  Comparator #(.mode("unsigned"), .width(7)) comparator_3 (
    .a(opcode), .b(7'b0000011), .eq(comparator_3_eq));  // open: gt, lt
  Comparator #(.mode("unsigned"), .width(3)) comparator_4 (
    .a(funct3), .b(3'b001), .eq(comparator_4_eq));  // open: gt, lt
  Comparator #(.mode("unsigned"), .width(7)) comparator_5 (
    .a(opcode), .b(7'b0000011), .eq(comparator_5_eq));  // open: gt, lt
  Comparator #(.mode("unsigned"), .width(3)) comparator_6 (
    .a(funct3), .b(3'b010), .eq(comparator_6_eq));  // open: gt, lt
  and and_1 (is_lb, comparator_1_eq, comparator_2_eq);
  and and_2 (is_lh, comparator_3_eq, comparator_4_eq);
  and and_3 (is_lw, comparator_5_eq, comparator_6_eq);
  Register #(.width(32)) register_2 (.D(PROGRAM_COUNTER), .en(1'b1), .clk(clk), .Q(PCforALU));  // open: clr
  control_logic control_logic_1 (
    .CSRWen(CSRWen), .PCSel(PCSel), .RegWEn(RegWEn), .ImmSel(ImmSel), .BrUn(BrUn), .ASel(ASel), .BSel(BSel),
    .ALUSel(ALUSel), .MemRW(MemRW), .WBSel(WBSel), .CSRSel(CSRSel),
    .inst({funct7, AddrB, AddrA, funct3, AddrD, opcode}), .BrEq(BrEq), .BrLt(BrLt));
  Comparator #(.mode("unsigned"), .width(7)) comparator_7 (
    .a(opcode), .b(7'b0100011), .eq(comparator_7_eq));  // open: gt, lt
  Comparator #(.mode("unsigned"), .width(3)) comparator_8 (
    .a(funct3), .b(3'b000), .eq(comparator_8_eq));  // open: gt, lt
  Comparator #(.mode("unsigned"), .width(7)) comparator_9 (
    .a(opcode), .b(7'b0100011), .eq(comparator_9_eq));  // open: gt, lt
  Comparator #(.mode("unsigned"), .width(3)) comparator_10 (
    .a(funct3), .b(3'b001), .eq(comparator_10_eq));  // open: gt, lt
  Comparator #(.mode("unsigned"), .width(7)) comparator_11 (
    .a(opcode), .b(7'b0100011), .eq(comparator_11_eq));  // open: gt, lt
  Comparator #(.mode("unsigned"), .width(3)) comparator_12 (
    .a(funct3), .b(3'b010), .eq(comparator_12_eq));  // open: gt, lt
  imm_gen imm_gen_1 (.inst({funct7, AddrB, AddrA, funct3, AddrD, opcode}), .ImmSel(ImmSel), .imm(imme));
  and and_4 (is_sb, comparator_7_eq, comparator_8_eq);
  and and_5 (is_sh, comparator_9_eq, comparator_10_eq);
  and and_6 (is_sw, comparator_11_eq, comparator_12_eq);
  Multiplexer #(.enable("false"), .width(4)) multiplexer_3 (
    .in0(4'b0000), .in1(4'b1111), .out(multiplexer_3_out), .sel(is_sw));
  Multiplexer #(.enable("false"), .width(32)) multiplexer_4 (
    .in0(READ_DATA_Byte), .in1(READ_DATA_Half_Word), .out(multiplexer_4_out), .sel(is_lh));
  regfile regfile_1 (
    .rs1(AddrA), .rs2(AddrB), .rd(AddrD), .Write_Data(WBResult), .RegWEn(RegWEn), .clk(clk), .ra(ra),
    .sp(sp), .t0(t0), .t1(t1), .t2(t2), .s0(s0), .s1(s1), .a0(a0), .Read_Data_1(DataA),
    .Read_Data_2(WRITE_DATA));
  branch_comp branch_comp_1 (.rs1(DataA), .rs2(WRITE_DATA), .BrUn(BrUn), .BrEq(BrEq), .BrLt(BrLt));
  Multiplexer #(.enable("false"), .width(4)) multiplexer_5 (
    .in0(multiplexer_3_out), .in1(4'b0011), .out(multiplexer_5_out), .sel(is_sh));
  Multiplexer #(.enable("false"), .width(4)) multiplexer_6 (
    .in0(multiplexer_5_out), .in1(4'b0001), .out(multiplexer_6_out), .sel(is_sb));
  assign READ_DATA_Byte = {{24{1'b0}}, READ_DATA[7:0]};  // Bit_Extender bit_extender_1
  assign READ_DATA_Half_Word = {{16{1'b0}}, READ_DATA[15:0]};  // Bit_Extender bit_extender_2
  Multiplexer #(.enable("false"), .width(4)) multiplexer_7 (
    .in0(4'b0000), .in1(multiplexer_6_out), .out(WRITE_ENABLE), .sel(MemRW));
  Multiplexer #(.enable("false"), .width(32)) multiplexer_8 (
    .in0(multiplexer_4_out), .in1(READ_DATA), .out(DMEM_WRITE_DATA), .sel(is_lw));
  Multiplexer #(.enable("false"), .width(32)) multiplexer_9 (
    .in0(DataA), .in1(imme), .out(multiplexer_9_out), .sel(CSRSel));
  Multiplexer #(.enable("false"), .width(32)) multiplexer_10 (
    .in0(DataA), .in1(PCforALU), .out(multiplexer_10_out), .sel(ASel));
  Multiplexer #(.enable("false"), .width(32)) multiplexer_11 (
    .in0(WRITE_DATA), .in1(imme), .out(multiplexer_11_out), .sel(BSel));
  alu alu_1 (.Result(WRITE_ADDRESS), .A(multiplexer_10_out), .B(multiplexer_11_out), .ALUSel(ALUSel));
  csr csr_1 (.CSR_address(12'h51e), .CSR_din(multiplexer_9_out), .CSR_WE(CSRWen), .clk(clk), .tohost(tohost));
  Multiplexer #(.enable("false"), .select(2), .width(32)) multiplexer_12 (
    .in0(DMEM_WRITE_DATA), .in1(WRITE_ADDRESS), .in2(PROGRAM_COUNTER), .in3(imme), .out(WBResult), .sel(WBSel));

  // Other names for the same wires on the sheet: ALUResult[31:0] = WRITE_ADDRESS; DataB[31:0] = WRITE_DATA;
  //   READ_DATA_Word[31:0] = READ_DATA

  // Notes on the sheet:
  //   Output to IMEM
  //   IMEM (do **NOT** move this)
  //   Inputs from IMEM
  //   It is OK to move the PC, RegFile, ALU, MEM, Branch Comp, Imm Gen, and Control Logic to wherever is most convenient for you when constructing your CPU, and to delete this text
  //   Inputs/Outputs for testing. Do **NOT** move these.
  //   Outputs To DMEM
  //   DMEM (do **NOT** move this)
  //   Inputs From DMEM
endmodule
