// Logisim project alu.circ as structural Verilog: 3 circuits, main circuit alu
module alu (
  input  [31:0] A,
  input  [31:0] B,
  input  [3:0] ALUSel,
  output [31:0] Result
);

  wire [0:0] slt7;
  wire [31:0] add0, and1, mul10, mulh14, mulhu11, multiplier_2_out, or2, sll6, sra5, srl4, sub12, xor3;
  wire [63:0] signed_extneder_1_extender_output, signed_extneder_2_extender_output,
       unsigned_extender_1_unsigned_extender_output, unsigned_extender_2_unsigned_extender_output;

  Adder #(.width(32)) adder_1 (.a(A), .b(B), .out(add0));  // open: cin, cout
  assign and1 = A & B;  // AND_Gate and_1, 32 bits wide
  assign or2 = A | B;  // OR_Gate or_1, 32 bits wide
  assign xor3 = A ^ B;  // XOR_Gate xor_1, 32 bits wide
  Shifter #(.shift("lr"), .width(32)) shifter_1 (.in(A), .\dist (B[4:0]), .out(srl4));
  Shifter #(.shift("ar"), .width(32)) shifter_2 (.in(A), .\dist (B[4:0]), .out(sra5));
  Shifter #(.width(32)) shifter_3 (.in(A), .\dist (B[4:0]), .out(sll6));
  Comparator #(.width(32)) comparator_1 (.a(A), .b(B), .lt(slt7[0]));  // open: gt, eq
  Subtractor #(.width(32)) subtractor_1 (.a(A), .b(B), .out(sub12));  // open: bin, bout
  signed_extneder signed_extneder_1 (.X(A), .extender_output(signed_extneder_1_extender_output));
  signed_extneder signed_extneder_2 (.X(B), .extender_output(signed_extneder_2_extender_output));
  unsigned_extender unsigned_extender_1 (
    .X(A), .unsigned_extender_output(unsigned_extender_1_unsigned_extender_output));
  unsigned_extender unsigned_extender_2 (
    .X(B), .unsigned_extender_output(unsigned_extender_2_unsigned_extender_output));
  Multiplier #(.mode("twosComplement"), .width(64)) multiplier_1 (
    .a(signed_extneder_1_extender_output), .b(signed_extneder_2_extender_output), .out({mulh14, mul10}));  // open: cin, cout
  Multiplier #(.mode("twosComplement"), .width(64)) multiplier_2 (
    .a(unsigned_extender_1_unsigned_extender_output), .b(unsigned_extender_2_unsigned_extender_output),
    .out({mulhu11, multiplier_2_out}));  // open: cin, cout
  Multiplexer #(.enable("false"), .select(4), .width(32)) multiplexer_1 (
    .in0(add0), .in1(and1), .in2(or2), .in3(xor3), .in4(srl4), .in5(sra5), .in6(sll6),
    .in7({{31{1'b0}}, slt7[0]}), .in8({32{1'b0}}), .in9({32{1'b0}}), .in10(mul10), .in11(mulhu11),
    .in12(sub12), .in13(B), .in14(mulh14), .in15({32{1'b0}}), .out(Result), .sel(ALUSel));

  // Other names for the same wires on the sheet: bsel13[31:0] = B

  // Notes on the sheet:
  //   INPUTS to your circuit
  //   DON'T CHANGE THE LOCATIONS OF THE INPUTS AND OUTPUTS!
  //   OUTPUT from your circuit
endmodule

module signed_extneder (
  input  [31:0] X,
  output [63:0] extender_output
);

  Multiplexer #(.enable("false"), .width(33)) multiplexer_1 (
    .in0({33{1'b0}}), .in1({33{1'b1}}), .out(extender_output[63:31]), .sel(X[31]));

  assign extender_output[30:0] = X[30:0];
endmodule

module unsigned_extender (
  input  [31:0] X,
  output [63:0] unsigned_extender_output
);


  assign unsigned_extender_output = {{32{1'b0}}, X};
endmodule
