// Logisim project control_logic.circ as structural Verilog: 1 circuit, main circuit control_logic
module control_logic (
  input  [31:0] inst,
  input  BrEq,
  input  BrLt,
  output PCSel,
  output RegWEn,
  output [2:0] ImmSel,
  output BrUn,
  output ASel,
  output BSel,
  output [3:0] ALUSel,
  output MemRW,
  output [1:0] WBSel,
  output CSRSel,
  output CSRWen
);

  wire and_1_out, and_2_out, and_3_out, and_4_out, and_5_out, and_6_out, comparator_1_eq, comparator_2_eq,
       comparator_3_eq, comparator_4_eq, comparator_5_eq, comparator_6_eq, comparator_7_eq, comparator_8_eq,
       comparator_9_eq, comparator_10_eq, comparator_11_eq, comparator_12_eq, comparator_13_eq,
       comparator_14_eq, comparator_16_eq, comparator_17_eq, comparator_18_eq, comparator_19_eq,
       comparator_20_eq, comparator_21_eq, comparator_22_eq, comparator_23_eq, comparator_24_eq,
       comparator_25_eq, comparator_26_eq, comparator_27_eq, comparator_28_eq, comparator_29_eq,
       comparator_30_eq, comparator_32_eq, comparator_33_eq, comparator_34_eq, comparator_37_eq,
       comparator_38_eq, comparator_41_eq, comparator_42_eq, comparator_43_eq, comparator_44_eq,
       comparator_48_eq, comparator_49_eq, is_auipc, is_beq, is_bge, is_bgeu, is_blt, is_bltu, is_bne,
       is_csrw, is_jal, is_jalr, is_load, is_lui, is_mul, is_mulh, is_mulhu, is_sra, is_sub, need_PCadd4,
       not_1_out, not_2_out, not_3_out, not_6_out, or_1_out, type_CSR, type_I, type_R, type_SB, type_U,
       type_UJ;
  wire [1:0] multiplexer_5_out, multiplexer_8_out;
  wire [2:0] multiplexer_1_out, multiplexer_3_out, multiplexer_6_out, multiplexer_9_out, multiplexer_12_out;
  wire [3:0] multiplexer_2_out, multiplexer_4_out, multiplexer_7_out, multiplexer_10_out, multiplexer_13_out,
       multiplexer_14_out;

  Multiplexer #(.enable("false"), .width(3)) multiplexer_1 (
    .in0(3'b000), .in1(3'b000), .out(multiplexer_1_out), .sel(type_I));
  Multiplexer #(.enable("false"), .select(3), .width(4)) multiplexer_2 (
    .in0(4'b0000), .in1(4'b0110), .in2(4'b0111), .in4(4'b0011), .in5(4'b0100), .in6(4'b0010), .in7(4'b0001),
    .out(multiplexer_2_out), .sel(inst[14:12]));  // open: in3
  or or_1 (or_1_out, MemRW, type_CSR, type_SB);
  Multiplexer #(.enable("false"), .width(3)) multiplexer_3 (
    .in0(multiplexer_1_out), .in1(3'b001), .out(multiplexer_3_out), .sel(MemRW));
  Multiplexer #(.enable("false"), .width(4)) multiplexer_4 (
    .in0(multiplexer_2_out), .in1(4'b1010), .out(multiplexer_4_out), .sel(is_mul));
  Multiplexer #(.enable("false"), .width(2)) multiplexer_5 (
    .in0(2'b01), .in1(2'b00), .out(multiplexer_5_out), .sel(is_load));
  not not_1 (not_1_out, BrEq);
  not not_2 (not_2_out, BrLt);
  not not_3 (not_3_out, BrLt);
  not not_4 (RegWEn, or_1_out);
  Multiplexer #(.enable("false"), .width(3)) multiplexer_6 (
    .in0(multiplexer_3_out), .in1(3'b010), .out(multiplexer_6_out), .sel(type_SB));
  Multiplexer #(.enable("false"), .width(4)) multiplexer_7 (
    .in0(multiplexer_4_out), .in1(4'b1011), .out(multiplexer_7_out), .sel(is_mulhu));
  not not_5 (BSel, type_R);
  Multiplexer #(.enable("false"), .width(2)) multiplexer_8 (
    .in0(multiplexer_5_out), .in1(2'b10), .out(multiplexer_8_out), .sel(need_PCadd4));
  or or_2 (BrUn, is_bltu, is_bgeu);
  and and_1 (and_1_out, is_beq, BrEq);
  and and_2 (and_2_out, is_bne, not_1_out);
  and and_3 (and_3_out, is_blt, BrLt);
  and and_4 (and_4_out, is_bge, not_2_out);
  and and_5 (and_5_out, is_bltu, BrLt);
  and and_6 (and_6_out, is_bgeu, not_3_out);
  Multiplexer #(.enable("false"), .width(3)) multiplexer_9 (
    .in0(multiplexer_6_out), .in1(3'b011), .out(multiplexer_9_out), .sel(type_U));
  Multiplexer #(.enable("false"), .width(4)) multiplexer_10 (
    .in0(multiplexer_7_out), .in1(4'b1110), .out(multiplexer_10_out), .sel(is_mulh));
  or or_3 (ASel, is_auipc, type_SB, is_jal);
  Multiplexer #(.enable("false"), .width(2)) multiplexer_11 (
    .in0(multiplexer_8_out), .in1(2'b11), .out(WBSel), .sel(is_lui));
  or or_4 (PCSel, is_jalr, and_1_out, and_2_out, and_3_out, and_4_out, and_5_out, and_6_out, is_jal);
  Multiplexer #(.enable("false"), .width(3)) multiplexer_12 (
    .in0(multiplexer_9_out), .in1(3'b100), .out(multiplexer_12_out), .sel(type_UJ));
  Multiplexer #(.enable("false"), .width(4)) multiplexer_13 (
    .in0(multiplexer_10_out), .in1(4'b1100), .out(multiplexer_13_out), .sel(is_sub));
  Multiplexer #(.enable("false"), .width(4)) multiplexer_14 (
    .in0(multiplexer_13_out), .in1(4'b0101), .out(multiplexer_14_out), .sel(is_sra));
  Multiplexer #(.enable("false"), .width(3)) multiplexer_15 (
    .in0(multiplexer_12_out), .in1(3'b101), .out(ImmSel), .sel(type_CSR));
  Multiplexer #(.enable("false"), .width(4)) multiplexer_16 (
    .in0(multiplexer_14_out), .in1(4'b0000), .out(ALUSel), .sel(not_6_out));
  not not_6 (not_6_out, type_R);
  Comparator #(.mode("unsigned"), .width(7)) comparator_1 (
    .a(inst[6:0]), .b(7'b1100011), .eq(comparator_1_eq));  // open: gt, lt
  Comparator #(.mode("unsigned"), .width(3)) comparator_2 (
    .a(inst[14:12]), .b(3'b000), .eq(comparator_2_eq));  // open: gt, lt
  Comparator #(.mode("unsigned"), .width(7)) comparator_3 (
    .a(inst[6:0]), .b(7'b1100011), .eq(comparator_3_eq));  // open: gt, lt
  Comparator #(.mode("unsigned"), .width(3)) comparator_4 (
    .a(inst[14:12]), .b(3'b001), .eq(comparator_4_eq));  // open: gt, lt
  Comparator #(.mode("unsigned"), .width(7)) comparator_5 (
    .a(inst[6:0]), .b(7'b1100011), .eq(comparator_5_eq));  // open: gt, lt
  Comparator #(.mode("unsigned"), .width(3)) comparator_6 (
    .a(inst[14:12]), .b(3'b100), .eq(comparator_6_eq));  // open: gt, lt
  Comparator #(.mode("unsigned"), .width(7)) comparator_7 (
    .a(inst[6:0]), .b(7'b1100011), .eq(comparator_7_eq));  // open: gt, lt
  Comparator #(.mode("unsigned"), .width(3)) comparator_8 (
    .a(inst[14:12]), .b(3'b101), .eq(comparator_8_eq));  // open: gt, lt
  Comparator #(.mode("unsigned"), .width(7)) comparator_9 (
    .a(inst[6:0]), .b(7'b1100011), .eq(comparator_9_eq));  // open: gt, lt
  Comparator #(.mode("unsigned"), .width(3)) comparator_10 (
    .a(inst[14:12]), .b(3'b110), .eq(comparator_10_eq));  // open: gt, lt
  Comparator #(.mode("unsigned"), .width(7)) comparator_11 (
    .a(inst[6:0]), .b(7'b1100011), .eq(comparator_11_eq));  // open: gt, lt
  Comparator #(.mode("unsigned"), .width(3)) comparator_12 (
    .a(inst[14:12]), .b(3'b111), .eq(comparator_12_eq));  // open: gt, lt
  and and_7 (is_beq, comparator_1_eq, comparator_2_eq);
  and and_8 (is_bne, comparator_3_eq, comparator_4_eq);
  and and_9 (is_blt, comparator_5_eq, comparator_6_eq);
  and and_10 (is_bge, comparator_7_eq, comparator_8_eq);
  and and_11 (is_bltu, comparator_9_eq, comparator_10_eq);
  and and_12 (is_bgeu, comparator_11_eq, comparator_12_eq);
  Comparator #(.mode("unsigned"), .width(7)) comparator_13 (
    .a(inst[6:0]), .b(7'b1101111), .eq(comparator_13_eq));  // open: gt, lt
  Comparator #(.mode("unsigned"), .width(7)) comparator_14 (
    .a(inst[6:0]), .b(7'b1100111), .eq(comparator_14_eq));  // open: gt, lt
  Comparator #(.mode("unsigned"), .width(7)) comparator_15 (
    .a(inst[6:0]), .b(7'b0000011), .eq(is_load));  // open: gt, lt
  Comparator #(.mode("unsigned"), .width(7)) comparator_16 (
    .a(inst[6:0]), .b(7'b0110011), .eq(comparator_16_eq));  // open: gt, lt
  Comparator #(.mode("unsigned"), .width(7)) comparator_17 (
    .a(inst[31:25]), .b(7'b0100000), .eq(comparator_17_eq));  // open: gt, lt
  Comparator #(.mode("unsigned"), .width(3)) comparator_18 (
    .a(inst[14:12]), .b(3'b000), .eq(comparator_18_eq));  // open: gt, lt
  Comparator #(.mode("unsigned"), .width(7)) comparator_19 (
    .a(inst[6:0]), .b(7'b0110011), .eq(comparator_19_eq));  // open: gt, lt
  Comparator #(.mode("unsigned"), .width(7)) comparator_20 (
    .a(inst[31:25]), .b(7'b0100000), .eq(comparator_20_eq));  // open: gt, lt
  Comparator #(.mode("unsigned"), .width(3)) comparator_21 (
    .a(inst[14:12]), .b(3'b101), .eq(comparator_21_eq));  // open: gt, lt
  Comparator #(.mode("unsigned"), .width(7)) comparator_22 (
    .a(inst[6:0]), .b(7'b0110011), .eq(comparator_22_eq));  // open: gt, lt
  Comparator #(.mode("unsigned"), .width(7)) comparator_23 (
    .a(inst[31:25]), .b(7'b0000001), .eq(comparator_23_eq));  // open: gt, lt
  Comparator #(.mode("unsigned"), .width(3)) comparator_24 (
    .a(inst[14:12]), .b(3'b000), .eq(comparator_24_eq));  // open: gt, lt
  Comparator #(.mode("unsigned"), .width(7)) comparator_25 (
    .a(inst[6:0]), .b(7'b0110011), .eq(comparator_25_eq));  // open: gt, lt
  Comparator #(.mode("unsigned"), .width(7)) comparator_26 (
    .a(inst[31:25]), .b(7'b0000001), .eq(comparator_26_eq));  // open: gt, lt
  Comparator #(.mode("unsigned"), .width(3)) comparator_27 (
    .a(inst[14:12]), .b(3'b001), .eq(comparator_27_eq));  // open: gt, lt
  Comparator #(.mode("unsigned"), .width(7)) comparator_28 (
    .a(inst[6:0]), .b(7'b0110011), .eq(comparator_28_eq));  // open: gt, lt
  Comparator #(.mode("unsigned"), .width(7)) comparator_29 (
    .a(inst[31:25]), .b(7'b0000001), .eq(comparator_29_eq));  // open: gt, lt
  Comparator #(.mode("unsigned"), .width(3)) comparator_30 (
    .a(inst[14:12]), .b(3'b011), .eq(comparator_30_eq));  // open: gt, lt
  Comparator #(.mode("unsigned"), .width(7)) comparator_31 (
    .a(inst[6:0]), .b(7'b0110011), .eq(type_R));  // open: gt, lt
  Comparator #(.mode("unsigned"), .width(7)) comparator_32 (
    .a(inst[6:0]), .b(7'b0000011), .eq(comparator_32_eq));  // open: gt, lt
  Comparator #(.mode("unsigned"), .width(7)) comparator_33 (
    .a(inst[6:0]), .b(7'b0010011), .eq(comparator_33_eq));  // open: gt, lt
  Comparator #(.mode("unsigned"), .width(7)) comparator_34 (
    .a(inst[6:0]), .b(7'b1100111), .eq(comparator_34_eq));  // open: gt, lt
  Comparator #(.mode("unsigned"), .width(7)) comparator_35 (.a(inst[6:0]), .b(7'b0100011), .eq(MemRW));  // open: gt, lt
  Comparator #(.mode("unsigned"), .width(7)) comparator_36 (
    .a(inst[6:0]), .b(7'b1100011), .eq(type_SB));  // open: gt, lt
  Comparator #(.mode("unsigned"), .width(7)) comparator_37 (
    .a(inst[6:0]), .b(7'b0010111), .eq(comparator_37_eq));  // open: gt, lt
  Comparator #(.mode("unsigned"), .width(7)) comparator_38 (
    .a(inst[6:0]), .b(7'b0110111), .eq(comparator_38_eq));  // open: gt, lt
  Comparator #(.mode("unsigned"), .width(7)) comparator_39 (
    .a(inst[6:0]), .b(7'b1101111), .eq(type_UJ));  // open: gt, lt
  Comparator #(.mode("unsigned"), .width(7)) comparator_40 (
    .a(inst[6:0]), .b(7'b1110011), .eq(type_CSR));  // open: gt, lt
  or or_5 (need_PCadd4, comparator_13_eq, comparator_14_eq);
  and and_13 (is_sub, comparator_16_eq, comparator_17_eq, comparator_18_eq);
  and and_14 (is_sra, comparator_19_eq, comparator_20_eq, comparator_21_eq);
  and and_15 (is_mul, comparator_22_eq, comparator_23_eq, comparator_24_eq);
  and and_16 (is_mulh, comparator_25_eq, comparator_26_eq, comparator_27_eq);
  and and_17 (is_mulhu, comparator_28_eq, comparator_29_eq, comparator_30_eq);
  or or_6 (type_I, comparator_32_eq, comparator_33_eq, comparator_34_eq);
  or or_7 (type_U, comparator_37_eq, comparator_38_eq);
  Comparator #(.mode("unsigned"), .width(7)) comparator_41 (
    .a(inst[6:0]), .b(7'b1110011), .eq(comparator_41_eq));  // open: gt, lt
  and and_18 (is_csrw, comparator_41_eq, comparator_42_eq);
  Comparator #(.mode("unsigned"), .width(3)) comparator_42 (
    .a(inst[14:12]), .b(3'b001), .eq(comparator_42_eq));  // open: gt, lt
  Comparator #(.mode("unsigned"), .width(7)) comparator_43 (
    .a(inst[6:0]), .b(7'b1110011), .eq(comparator_43_eq));  // open: gt, lt
  and and_19 (CSRSel, comparator_43_eq, comparator_44_eq);
  Comparator #(.mode("unsigned"), .width(3)) comparator_44 (
    .a(inst[14:12]), .b(3'b101), .eq(comparator_44_eq));  // open: gt, lt
  Comparator #(.mode("unsigned"), .width(7)) comparator_45 (
    .a(inst[6:0]), .b(7'b0010111), .eq(is_auipc));  // open: gt, lt
  Comparator #(.mode("unsigned"), .width(7)) comparator_46 (
    .a(inst[6:0]), .b(7'b1101111), .eq(is_jal));  // open: gt, lt
  Comparator #(.mode("unsigned"), .width(7)) comparator_47 (
    .a(inst[6:0]), .b(7'b0110111), .eq(is_lui));  // open: gt, lt
  Comparator #(.mode("unsigned"), .width(7)) comparator_48 (
    .a(inst[6:0]), .b(7'b1100111), .eq(comparator_48_eq));  // open: gt, lt
  and and_20 (is_jalr, comparator_48_eq, comparator_49_eq);
  Comparator #(.mode("unsigned"), .width(3)) comparator_49 (
    .a(inst[14:12]), .b(3'b000), .eq(comparator_49_eq));  // open: gt, lt

  assign CSRWen = 1'b1;

  // Other names for the same wires on the sheet: opcode[6:0] = inst[6:0]; funct3[2:0] = inst[14:12];
  //   funct7[6:0] = inst[31:25]; is_csrwi = CSRSel; type_S = MemRW

  // Notes on the sheet:
  //   INPUTS to your circuit
  //   DON'T CHANGE THE LOCATIONS OF THE INPUTS AND OUTPUTS!
  //   OUTPUT from your circuit
endmodule
