// Logisim project cpu.circ as structural Verilog: 1 circuit, main circuit cpu
module cpu (
  input  clk,
  input  [31:0] INSTRUCTION,
  input  [31:0] READ_DATA,
  output [31:0] WRITE_ADDRESS,
  output [31:0] PROGRAM_COUNTER,
  output [31:0] ra,
  output [31:0] sp,
  output [31:0] t0,
  output [31:0] t1,
  output [31:0] t2,
  output [31:0] s0,
  output [31:0] s1,
  output [31:0] a0,
  output [31:0] tohost,
  output [3:0] WRITE_ENABLE,
  output [31:0] WRITE_DATA
);

  wire ASel, BSel, RegWEn;
  wire [1:0] WBSel;
  wire [4:0] AddrA, AddrB, AddrD;
  wire [31:0] adder_1_out, ALUResult, DataA, DataB, imme, multiplexer_1_out, multiplexer_2_out, PCforALU,
       register_1_q, WBResult;

  Register #(.width(32)) register_1 (
    .D(INSTRUCTION), .en(1'b1), .clk(clk),
    .Q({register_1_q[31:25], AddrB, AddrA, register_1_q[14:12], AddrD, register_1_q[6:0]}));  // open: clr
  Adder #(.width(32)) adder_1 (.a(PROGRAM_COUNTER), .b(32'h4), .out(adder_1_out));  // open: cin, cout
  Register #(.width(32)) PC (.D(adder_1_out), .clk(clk), .Q(PROGRAM_COUNTER));  // open: en, clr
  Register #(.width(32)) register_2 (.D(PROGRAM_COUNTER), .en(1'b1), .clk(clk), .Q(PCforALU));  // open: clr
  control_logic control_logic_1 (
    .RegWEn(RegWEn), .ASel(ASel), .BSel(BSel), .WBSel(WBSel),
    .inst({register_1_q[31:25], AddrB, AddrA, register_1_q[14:12], AddrD, register_1_q[6:0]}));  // open: CSRWen, PCSel, ImmSel, BrUn, ALUSel, MemRW, CSRSel, BrEq, BrLt
  imm_gen imm_gen_1 (
    .inst({register_1_q[31:25], AddrB, AddrA, register_1_q[14:12], AddrD, register_1_q[6:0]}),
    .ImmSel(register_1_q[6:4]), .imm(imme));
  regfile regfile_1 (
    .rs1(AddrA), .rs2(AddrB), .rd(AddrD), .Write_Data(WBResult), .RegWEn(1'b1), .clk(clk), .ra(ra), .sp(sp),
    .t0(t0), .t1(t1), .t2(t2), .s0(s0), .s1(s1), .a0(a0), .Read_Data_1(DataA), .Read_Data_2(DataB));
  branch_comp branch_comp_1 (.rs1(DataA), .rs2(DataB));  // open: BrUn, BrEq, BrLt
  Multiplexer #(.enable("false"), .width(32)) multiplexer_1 (
    .in0(DataA), .in1(PROGRAM_COUNTER), .out(multiplexer_1_out), .sel(1'b0));
  Multiplexer #(.enable("false"), .width(32)) multiplexer_2 (
    .in0(DataB), .in1(imme), .out(multiplexer_2_out), .sel(1'b1));
  csr csr_1 (.tohost(tohost));  // open: CSR_address, CSR_din, CSR_WE, clk
  alu alu_1 (.Result(ALUResult), .A(multiplexer_1_out), .B(multiplexer_2_out));  // open: ALUSel
  Multiplexer #(.enable("false"), .select(2), .width(32)) multiplexer_3 (
    .in1(ALUResult), .out(WBResult), .sel(2'b01));  // open: in0, in2, in3

  // Notes on the sheet:
  //   Output to IMEM
  //   IMEM (do **NOT** move this)
  //   Inputs from IMEM
  //   It is OK to move the PC, RegFile, ALU, MEM, Branch Comp, Imm Gen, and Control Logic to wherever is most convenient for you when constructing your CPU, and to delete this text
  //   Inputs/Outputs for testing. Do **NOT** move these.
  //   Outputs To DMEM
  //   DMEM (do **NOT** move this)
  //   Inputs From DMEM
endmodule
